# Fritzing sketch IR.Receiver.TSOP312__.TSOP314__ (saved by Fritzing 0.9.2b)
circuit board: 3.4cm x 1.4cm
breadboards: 1

parts:
  PART1 = SparkFun Block for Intel Edison - GPIO [part_number=DEV-13038]
  IR1 = TSOP312.., 314.. [package=THT]
  C1 = Electrolytic Capacitor [capacitance=100µF package="100 mil [THT, electrolytic]"]
  R1 = Resistor [tolerance=±5% resistance=330 package=THT]
  R2 = Resistor [tolerance=±5% resistance=1k package=THT]

nets:
  GND: PART1.GND, IR1.GND, C1.-
  N1: PART1.VSYS, R1.Pin_1, R2.Pin_1
  N2: PART1.GP48, IR1.Data, R2.Pin_0
  N3: IR1.Vs, C1.+, R1.Pin_0

custom parts:
  SparkFun Block for Intel Edison - GPIO: The Intel® Edison is an ultra small computing platform that will change the way you look at embedded electronics. Each Edison is packed with a huge amount of tech goodies into a tiny package while still providing the same robust strength of your go-to single board computer. Powered by the Intel® Atom™ SoC dual-core CPU and including an integrated WiFi, Bluetooth LE, and a 70-pin connector to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
